// Logisim project 8-bit ALU ph1.circ as structural Verilog: 1 circuit, main circuit main
module main (
  input  [7:0] A,
  input  [7:0] B,
  input  [3:0] in_3,
  output [7:0] out_4,
  output out_5,
  output out_6,
  output out_7,
  output out_8,
  output out_9
);

  wire or_2_out;
  wire [7:0] adder_1_out, adder_2_out, adder_3_out, adder_4_out, adder_5_out, and_1_out, not_1_out, or_1_out,
       shifter_1_out, shifter_2_out;

  assign not_1_out = ~B;  // NOT_Gate not_1, 8 bits wide
  Adder adder_1 (.a(not_1_out), .b(8'h1), .out(adder_1_out));  // open: cin, cout
  Adder adder_2 (.a(A), .b(8'h1), .out(adder_2_out));  // open: cin, cout
  Adder adder_3 (.a(B), .b(8'h1), .out(adder_3_out));  // open: cin, cout
  Adder adder_4 (.a(A), .b(B), .out(adder_4_out));  // open: cin, cout
  Adder adder_5 (.a(A), .b(adder_1_out), .out(adder_5_out));  // open: cin, cout
  Shifter #(.shift("lr")) shifter_1 (.in(A), .\dist (3'b001), .out(shifter_1_out));
  Shifter shifter_2 (.in(A), .\dist (3'b001), .out(shifter_2_out));
  assign and_1_out = A & B;  // AND_Gate and_1, 8 bits wide
  assign or_1_out = A | B;  // OR_Gate or_1, 8 bits wide
  Multiplexer #(.select(4), .width(8)) multiplexer_1 (
    .in0(A), .in1(B), .in2(adder_2_out), .in3(adder_3_out), .in4(adder_4_out), .in5(adder_5_out),
    .in6(shifter_1_out), .in7(shifter_2_out), .in8(and_1_out), .in9(or_1_out), .out(out_4), .sel(in_3));  // open: in10, in11, in12, in13, in14, in15, en
  Comparator comparator_1 (.a(out_4), .b(B), .gt(out_5), .eq(out_6), .lt(out_7));
  or or_2 (or_2_out, out_4[0], out_4[1], out_4[2], out_4[3], out_4[4], out_4[5], out_4[6], out_4[7]);
  not not_2 (out_8, or_2_out);

  assign out_9 = out_4[7];
endmodule
