// Logisim project 8-bit ALU ph1_2.circ as structural Verilog: 1 circuit, main circuit main
module main (
  input  [7:0] A,
  input  [7:0] B,
  input  [3:0] in_3,
  output [7:0] out_4,
  output out_5,
  output out_6,
  output out_7,
  output out_8,
  output [3:0] out_9
);

  wire comparator_1_eq, comparator_1_gt, comparator_1_lt, or_2_out;
  wire [3:0] and_3_out, and_4_out, not_2_out, not_3_out;
  wire [3:1] undriven, undriven_2, undriven_3, undriven_4;
  wire [7:0] adder_1_out, adder_2_out, adder_3_out, and_1_out, and_2_out, not_1_out, or_1_out, shifter_1_out,
       shifter_2_out, xor_1_out;

  Adder adder_1 (.a(A), .b(8'h1), .out(adder_1_out));  // open: cin, cout
  Adder adder_2 (.a(A), .b(8'h1), .out(adder_2_out));  // open: cin, cout
  assign xor_1_out = B ^ and_2_out;  // XOR_Gate xor_1, 8 bits wide
  assign not_1_out = ~A;  // NOT_Gate not_1, 8 bits wide
  assign and_1_out = A & B;  // AND_Gate and_1, 8 bits wide
  assign or_1_out = A | B;  // OR_Gate or_1, 8 bits wide
  Adder adder_3 (.a(A), .b(xor_1_out), .out(adder_3_out), .cout(out_8));  // open: cin
  assign and_2_out[3:0] = and_3_out & and_4_out;  // AND_Gate and_2, 4 bits wide
  Shifter #(.shift("lr")) shifter_1 (.in(A), .\dist (3'b001), .out(shifter_1_out));
  Shifter shifter_2 (.in(A), .\dist (3'b001), .out(shifter_2_out));
  assign and_3_out = {undriven, out_9[0]} & not_2_out;  // AND_Gate and_3, 4 bits wide
  assign and_4_out = not_3_out & {undriven_4, out_9[3]};  // AND_Gate and_4, 4 bits wide
  assign not_2_out = ~{undriven_2, out_9[1]};  // NOT_Gate not_2, 4 bits wide
  assign not_3_out = ~{undriven_3, out_9[2]};  // NOT_Gate not_3, 4 bits wide
  Multiplexer #(.select(4), .width(8)) multiplexer_1 (
    .in0(adder_3_out), .in1(adder_1_out), .in2(adder_2_out), .in3(A), .in4(not_1_out), .in5(and_1_out),
    .in6(or_1_out), .in7(shifter_1_out), .in8(shifter_2_out), .in9(adder_3_out), .out(out_4), .sel(out_9));  // open: in10, in11, in12, in13, in14, in15, en
  Comparator comparator_1 (.a(out_4), .b(B), .gt(comparator_1_gt), .eq(comparator_1_eq), .lt(comparator_1_lt));
  or or_2 (or_2_out, out_4[0], out_4[1], out_4[2], out_4[3], out_4[4], out_4[5], out_4[6], out_4[7]);
  not not_4 (out_5, or_2_out);
  // Pins of 1 and 4 bits meet at {undriven_3, out_9[2]}
  // Pins of 1 and 4 bits meet at {undriven, out_9[0]}
  // Pins of 1 and 4 bits meet at {undriven_2, out_9[1]}
  // Pins of 4 and 8 bits meet at and_2_out
  // Pins of 1 and 4 bits meet at {undriven_4, out_9[3]}

  assign out_6 = out_4[7];
endmodule
