// Logisim project 8-bit ALU ph2.circ as structural Verilog: 1 circuit, main circuit main
module main (
  input  [7:0] A,
  input  [7:0] B,
  input  [3:0] Opcodes,
  output [7:0] out_4,
  output out_5,
  output out_6,
  output out_7,
  output Zero,
  output Negative
);

  wire OR_2_out;
  wire [7:0] adder_1_out, adder_2_out, adder_3_out, adder_4_out, AND_out, not_1_out, OR_out, shifter_1_out,
       shifter_2_out, subtractor_1_out;

  assign not_1_out = ~B;  // NOT_Gate not_1, 8 bits wide
  Adder adder_1 (.a(not_1_out), .b(8'h1), .out(adder_1_out));  // open: cin, cout
  Adder adder_2 (.a(A), .b(8'h1), .out(adder_2_out));  // open: cin, cout
  Subtractor subtractor_1 (.a(B), .b(8'h1), .out(subtractor_1_out));  // open: bin, bout
  Adder adder_3 (.a(A), .b(B), .out(adder_3_out));  // open: cin, cout
  Adder adder_4 (.a(A), .b(adder_1_out), .out(adder_4_out));  // open: cin, cout
  Shifter #(.shift("lr")) shifter_1 (.in(A), .\dist (3'b001), .out(shifter_1_out));
  Shifter shifter_2 (.in(A), .\dist (3'b001), .out(shifter_2_out));
  assign AND_out = A & B;  // AND_Gate AND, 8 bits wide
  assign OR_out = A | B;  // OR_Gate OR, 8 bits wide
  Multiplexer #(.select(4), .width(8)) multiplexer_1 (
    .in0(A), .in1(B), .in2(adder_2_out), .in3(subtractor_1_out), .in4(adder_3_out), .in5(adder_4_out),
    .in6(shifter_1_out), .in7(shifter_2_out), .in8(AND_out), .in9(OR_out), .out({Negative, out_4[6:0]}),
    .sel(Opcodes));  // open: in10, in11, in12, in13, in14, in15, en
  Comparator comparator_1 (.a({Negative, out_4[6:0]}), .b(B), .gt(out_5), .eq(out_6), .lt(out_7));
  or OR_2 (OR_2_out, out_4[0], out_4[1], out_4[2], out_4[3], out_4[4], out_4[5], out_4[6], Negative);
  not not_2 (Zero, OR_2_out);

  assign out_4[7] = Negative;

  // Notes on the sheet:
  //   1) 0001 = Increment
  //   2) 0010 = Decrement
  //   5) 0101 = Subtract
  //   6) 0110 = Register right logic shift
  //   7) 0111 = Register left logic shift
  //   8) 1000 = Logic bitwise And
  //   9) 1001 = Logic bitwise Or
  //   0) 0000 = Arithmetic Addition
  //   1) 0001 = Increment input A by 1
  //   2) 0010 = Decrement input by 1
  //   3) 0011 = Comparison between A and B
  //   4) 0100 = Logic bitwise Not of "A"
  //   5) 0101 = Subtract
  //   6) 0110 = Register right logic shift
  //   7) 0111 = Register left logic shift
  //   8) 1000 = Logic bitwise And
  //   9) 1001 = Logic bitwise Or
  //   Result (in 2 complements)
  //   3) 0011 = Comparison
endmodule
