// Logisim project Controller ph3.circ as structural Verilog: 1 circuit, main circuit main
module main (
  input  [7:0] OpCodeIn,
  input  [7:0] in_2,
  input  [7:0] in_3,
  input  [3:0] ALU_Flags,
  input  Enable,
  input  Reset
);

  wire and_1_out, and_2_out, and_3_out, button_1_out, button_2_out, clock_1_out, comparator_1_eq,
       decoder_1_out0, decoder_1_out1, decoder_1_out2, decoder_1_out3, demultiplexer_1_out0,
       demultiplexer_1_out1, demultiplexer_1_out2, demultiplexer_1_out3, demultiplexer_1_out4,
       demultiplexer_1_out5, demultiplexer_1_out6, demultiplexer_1_out7, demultiplexer_1_out8,
       demultiplexer_1_out9, demultiplexer_1_out10, demultiplexer_1_out11, demultiplexer_1_out12,
       demultiplexer_1_out13, demultiplexer_1_out14, demultiplexer_1_out15, not_1_out, or_1_out, or_2_out,
       or_3_out, or_4_out;
  wire [1:0] t_ff_1_q;
  wire [7:0] Address_q, controlled_buffer_1_out, counter_1_q, multiplexer_1_out, OpCode_q;

  Button button_1 (.out(button_1_out));
  and and_1 (and_1_out, Enable, clock_1_out);
  Clock clock_1 (.out(clock_1_out));
  Register Address (.D(OpCodeIn), .en(decoder_1_out1), .Q(Address_q), .clk(decoder_1_out1), .clr(Reset));
  Register OpCode (.D(OpCodeIn), .en(decoder_1_out2), .Q(OpCode_q), .clk(decoder_1_out2), .clr(Reset));
  not not_1 (not_1_out, or_1_out);
  T_Flip_Flop t_ff_1 (.clk(or_1_out), .T(or_1_out), .Q(t_ff_1_q[0]), .reset(Reset));  // open: Qn, preset, en
  or or_1 (or_1_out, button_1_out, and_1_out);
  T_Flip_Flop t_ff_2 (.clk(t_ff_1_q[0]), .T(t_ff_1_q[0]), .Q(t_ff_1_q[1]), .reset(Reset));  // open: Qn, preset, en
  Decoder #(.select(2)) decoder_1 (
    .out0(decoder_1_out0), .out1(decoder_1_out1), .out2(decoder_1_out2), .out3(decoder_1_out3),
    .sel(t_ff_1_q), .en(not_1_out));
  Demultiplexer #(.select(4)) demultiplexer_1 (
    .out0(demultiplexer_1_out0), .out1(demultiplexer_1_out1), .out2(demultiplexer_1_out2),
    .out3(demultiplexer_1_out3), .out4(demultiplexer_1_out4), .out5(demultiplexer_1_out5),
    .out6(demultiplexer_1_out6), .out7(demultiplexer_1_out7), .out8(demultiplexer_1_out8),
    .out9(demultiplexer_1_out9), .out10(demultiplexer_1_out10), .out11(demultiplexer_1_out11),
    .out12(demultiplexer_1_out12), .out13(demultiplexer_1_out13), .out14(demultiplexer_1_out14),
    .out15(demultiplexer_1_out15), .in(comparator_1_eq), .sel(OpCode_q[7:4]), .en(decoder_1_out0));
  Comparator #(.width(4)) comparator_1 (.a(4'b0000), .b(OpCode_q[3:0]), .eq(comparator_1_eq));  // open: gt, lt
  and and_2 (and_2_out, ALU_Flags[2], demultiplexer_1_out3);
  or or_2 (or_2_out, decoder_1_out2, decoder_1_out3);
  and and_3 (and_3_out, ALU_Flags[3], demultiplexer_1_out2);
  or or_3 (or_3_out, and_2_out, and_3_out, demultiplexer_1_out1, button_2_out);
  or or_4 (or_4_out, or_2_out, or_3_out);
  Button button_2 (.out(button_2_out));
  Counter counter_1 (
    .load(or_3_out), .D(Address_q), .count(or_2_out), .Q(counter_1_q), .clk(or_4_out), .clr(Reset));  // open: carry
  assign controlled_buffer_1_out = decoder_1_out0 ? OpCode_q : 8'bz;  // Controlled_Buffer controlled_buffer_1
  Pull_Resistor pull_resistor_1 (.node(controlled_buffer_1_out));
  Multiplexer #(.width(8)) multiplexer_1 (
    .in0(counter_1_q), .in1(Address_q), .out(multiplexer_1_out), .sel(decoder_1_out0));  // open: en
endmodule
